// Logisim project cpu.circ as structural Verilog: 10 circuits, main circuit main
module main (
  input  reset
);

  wire add, addi, alu_1_rsgeqz, and_1_out, and_2_out, and_4636bc62, beq, bgez, branch, clk, ImmediateReg2,
       input_, j, jal, jr, jump, keyboard_1_avail, lw, memory_latch_1_oe_latched, memory_latch_1_we_latched,
       not_e3735ab1, NOTclk, output_, printtoRt, ReadWord, rsgeq0, rsISrt, sll_da58c505, srl_50f051ba, sub,
       sw, WriteEnableOn;
  wire [2:0] multiplexer_6_out, multiplexer_7_out;
  wire [3:0] ALUoptype, opcode;
  wire [6:0] bit_extender_2_out;
  wire [7:0] KeyboardOut;
  wire [11:0] adress;
  wire [15:0] ALUOutputData, jumparoundbranch_result, memory_latch_1_address_latched,
       memory_latch_1_data_in_latched, multiplexer_1_out, multiplexer_2_out, multiplexer_3_out,
       multiplexer_4_out, multiplexer_5_out, multiplexer_8_out, multiplexer_9_out, outputRs, outputRt,
       PC_dataout, PCplus1, ram_1_dout, SXimmediate;

  Clock clock_1 (.out(clk));
  Multiplexer #(.width(16), .enable("false")) multiplexer_1 (
    .in0({4'b0000, adress}), .in1(outputRs), .out(multiplexer_1_out), .sel(jr));
  not not_1 (NOTclk, clk);
  assign SXimmediate = {{10{adress[5]}}, adress[5:0]};  // Bit_Extender bit_extender_1
  Multiplexer #(.width(16), .enable("false")) multiplexer_2 (
    .in0(PCplus1), .in1(jumparoundbranch_result), .out(multiplexer_2_out), .sel(branch));
  Multiplexer #(.width(16), .enable("false")) multiplexer_3 (
    .in0(multiplexer_2_out), .in1(multiplexer_1_out), .out(multiplexer_3_out), .sel(jump));
  // Probe on PC_dataout
  ROM #(.addrWidth(16), .dataWidth(16)) rom_1 (.addr(PC_dataout), .data({opcode, adress}));
  singleregister PC (.dataIn(multiplexer_3_out), .clk(NOTclk), .writeEnable(1'b1), .reset(reset), .dataOut(PC_dataout));
  Keyboard keyboard_1 (.clk(NOTclk), .re(input_), .clr(reset), .avail(keyboard_1_avail), .data(KeyboardOut[6:0]));
  my_adder my_adder_1 (.B(16'h1), .A(PC_dataout), .result(PCplus1));  // open: sub, ovf
  my_adder jumparoundbranch (.B(SXimmediate), .A(PCplus1), .result(jumparoundbranch_result));  // open: sub, ovf
  not not_2 (KeyboardOut[7], keyboard_1_avail);
  // Probe on {{8{1'b0}}, KeyboardOut}
  // Probe on PC_dataout
  // Probe on {opcode, adress}
  // Probe on KeyboardOut[6:0]
  // Probe on bit_extender_2_out
  Bit_Extender #(.in_width(16), .out_width(7)) bit_extender_2 (.in(outputRs), .out(bit_extender_2_out));
  TTY #(.rows(13), .cols(80)) tty_1 (.data(bit_extender_2_out), .clk(clk), .we(output_), .clr(reset));
  Multiplexer #(.width(16), .enable("false")) multiplexer_4 (
    .in0(multiplexer_5_out), .in1({{8{1'b0}}, KeyboardOut}), .out(multiplexer_4_out), .sel(input_));
  // Probe on adress[8:6]
  Multiplexer #(.width(16), .enable("false")) multiplexer_5 (
    .in0(multiplexer_9_out), .in1(PCplus1), .out(multiplexer_5_out), .sel(jal));
  // Probe on adress[11:9]
  Multiplexer #(.width(3), .enable("false")) multiplexer_6 (
    .in0(adress[5:3]), .in1(adress[8:6]), .out(multiplexer_6_out), .sel(printtoRt));
  // Probe on opcode
  Multiplexer #(.width(3), .enable("false")) multiplexer_7 (
    .in0(multiplexer_6_out), .in1(3'b111), .out(multiplexer_7_out), .sel(jal));
  Decoder #(.select(4)) decoder_1 (
    .out0(addi), .out1(sub), .out2(add), .out3(not_e3735ab1), .out4(and_4636bc62), .out5(sll_da58c505),
    .out6(srl_50f051ba), .out7(lw), .out8(sw), .out9(bgez), .out10(beq), .out11(j), .out12(jr), .out13(jal),
    .out14(input_), .out15(output_), .sel(opcode));  // open: en
  or or_1 (ReadWord, lw, input_);
  RegisterFile registerfile_1 (
    .clk(clk), .reset(reset), .WriteData(multiplexer_4_out), .RegWriteEnable(WriteEnableOn),
    .ReadReg1(adress[11:9]), .ReadReg2(adress[8:6]), .WritePort(multiplexer_7_out), .Reg1Contents(outputRs),
    .Reg2Contents(outputRt));
  or or_2 (printtoRt, addi, lw);
  or or_3 (WriteEnableOn, addi, sub, add, not_e3735ab1, and_4636bc62, sll_da58c505, srl_50f051ba, lw, jal, input_);
  Multiplexer #(.width(16), .enable("false")) multiplexer_8 (
    .in0(outputRt), .in1(SXimmediate), .out(multiplexer_8_out), .sel(ImmediateReg2));
  // Probe on multiplexer_8_out
  or or_4 (ImmediateReg2, addi, lw, sw, bgez);
  // Probe on ALUoptype
  or or_5 (ALUoptype[3], sw, bgez, beq, j, jr, jal, input_, output_);
  or or_6 (ALUoptype[2], and_4636bc62, sll_da58c505, srl_50f051ba, lw, jr, jal, input_, output_);
  ALU alu_1 (
    .InputData1(outputRs), .InputData2(multiplexer_8_out), .ALUOpType(ALUoptype), .sham(adress[2:0]),
    .OutputData(ALUOutputData), .isZero(rsISrt), .rsgeqz(alu_1_rsgeqz));
  memory_latch memory_latch_1 (
    .address(ALUOutputData), .WE(sw), .clk(NOTclk), .data_in(outputRt),
    .address_latched(memory_latch_1_address_latched), .WE_latched(memory_latch_1_we_latched),
    .OE_latched(memory_latch_1_oe_latched), .data_in_latched(memory_latch_1_data_in_latched));
  or or_7 (ALUoptype[1], add, not_e3735ab1, srl_50f051ba, lw, beq, j, input_, output_);
  or or_8 (ALUoptype[0], sub, not_e3735ab1, sll_da58c505, lw, bgez, j, jal, output_);
  // Probe on rsgeq0
  not not_3 (rsgeq0, alu_1_rsgeqz);
  RAM #(.addrWidth(16), .dataWidth(16), .trigger("high"), .databus("bibus")) ram_1 (
    .addr(memory_latch_1_address_latched), .we(memory_latch_1_we_latched), .oe(memory_latch_1_oe_latched),
    .din(memory_latch_1_data_in_latched), .dout(ram_1_dout));
  // Probe on ALUOutputData
  and and_1 (and_1_out, rsgeq0, bgez);
  and and_2 (and_2_out, beq, rsISrt);
  or or_9 (branch, and_1_out, and_2_out);
  or or_10 (jump, j, jr, jal);
  // Probe on branch
  Multiplexer #(.width(16), .enable("false")) multiplexer_9 (
    .in0(ALUOutputData), .in1(ram_1_dout), .out(multiplexer_9_out), .sel(ReadWord));

  // Other names for the same wires on the sheet: immediate[5:0] = adress[5:0]; L[11:0] = adress;
  //   Shamt[2:0] = adress[2:0]; Rd[2:0] = adress[5:3]; Rt[2:0] = adress[8:6]; Rs[2:0] = adress[11:9]

  // Notes on the sheet:
  //   contents of rom_1 (hex, n*v repeats v):
  //   4a e008 2a0 f400 e008 2a0 f400 e008 2a0 f400 903f 903f 19e 903f 19f 903f 41 144 9202 198 903f 145
endmodule

module singleregister (
  input  [15:0] dataIn,
  input  clk,
  input  writeEnable,
  input  reset,
  output [15:0] dataOut
);

  wire clk_t;

  and and_1 (clk_t, clk, writeEnable);
  D_Flip_Flop d_ff_1 (.D(dataIn[0]), .clk(clk_t), .Q(dataOut[0]), .reset(reset));  // open: Qn, preset
  D_Flip_Flop d_ff_2 (.D(dataIn[1]), .clk(clk_t), .Q(dataOut[1]), .reset(reset));  // open: Qn, preset
  D_Flip_Flop d_ff_3 (.D(dataIn[2]), .clk(clk_t), .Q(dataOut[2]), .reset(reset));  // open: Qn, preset
  D_Flip_Flop d_ff_4 (.D(dataIn[3]), .clk(clk_t), .Q(dataOut[3]), .reset(reset));  // open: Qn, preset
  D_Flip_Flop d_ff_5 (.D(dataIn[4]), .clk(clk_t), .Q(dataOut[4]), .reset(reset));  // open: Qn, preset
  D_Flip_Flop d_ff_6 (.D(dataIn[5]), .clk(clk_t), .Q(dataOut[5]), .reset(reset));  // open: Qn, preset
  D_Flip_Flop d_ff_7 (.D(dataIn[6]), .clk(clk_t), .Q(dataOut[6]), .reset(reset));  // open: Qn, preset
  D_Flip_Flop d_ff_8 (.D(dataIn[7]), .clk(clk_t), .Q(dataOut[7]), .reset(reset));  // open: Qn, preset
  D_Flip_Flop d_ff_9 (.D(dataIn[8]), .clk(clk_t), .Q(dataOut[8]), .reset(reset));  // open: Qn, preset
  D_Flip_Flop d_ff_10 (.D(dataIn[9]), .clk(clk_t), .Q(dataOut[9]), .reset(reset));  // open: Qn, preset
  D_Flip_Flop d_ff_11 (.D(dataIn[10]), .clk(clk_t), .Q(dataOut[10]), .reset(reset));  // open: Qn, preset
  D_Flip_Flop d_ff_12 (.D(dataIn[11]), .clk(clk_t), .Q(dataOut[11]), .reset(reset));  // open: Qn, preset
  D_Flip_Flop d_ff_13 (.D(dataIn[12]), .clk(clk_t), .Q(dataOut[12]), .reset(reset));  // open: Qn, preset
  D_Flip_Flop d_ff_14 (.D(dataIn[13]), .clk(clk_t), .Q(dataOut[13]), .reset(reset));  // open: Qn, preset
  D_Flip_Flop d_ff_15 (.D(dataIn[14]), .clk(clk_t), .Q(dataOut[14]), .reset(reset));  // open: Qn, preset
  D_Flip_Flop d_ff_16 (.D(dataIn[15]), .clk(clk_t), .Q(dataOut[15]), .reset(reset));  // open: Qn, preset

  // Other names for the same wires on the sheet: in0 = dataIn[0]; in1 = dataIn[1]; in2 = dataIn[2]; in3 = dataIn[3];
  //   in4 = dataIn[4]; in5 = dataIn[5]; in6 = dataIn[6]; in7 = dataIn[7]; in8 = dataIn[8]; in9 = dataIn[9];
  //   in10 = dataIn[10]; in11 = dataIn[11]; in12 = dataIn[12]; in13 = dataIn[13]; in14 = dataIn[14];
  //   in15 = dataIn[15]; out0 = dataOut[0]; out1 = dataOut[1]; out2 = dataOut[2]; out3 = dataOut[3];
  //   out4 = dataOut[4]; out5 = dataOut[5]; out6 = dataOut[6]; out7 = dataOut[7]; out8 = dataOut[8];
  //   out9 = dataOut[9]; out10 = dataOut[10]; out11 = dataOut[11]; out12 = dataOut[12]; out13 = dataOut[13];
  //   out14 = dataOut[14]; out15 = dataOut[15]
endmodule

module RegisterFile (
  input  clk,
  input  reset,
  input  [15:0] WriteData,
  input  RegWriteEnable,
  input  [2:0] ReadReg1,
  input  [2:0] ReadReg2,
  input  [2:0] WritePort,
  output [15:0] Reg1Contents,
  output [15:0] Reg2Contents
);

  wire out1bit0, out1bit1, out1bit2, out1bit3, out1bit4, out1bit5, out1bit6, out1bit7, out2bit0, out2bit1,
       out2bit2, out2bit3, out2bit4, out2bit5, out2bit6, out2bit7, WE1, WE2, WE3, WE4, WE5, WE6, WE7;
  wire [15:0] singleregister_1_dataout, singleregister_2_dataout, singleregister_3_dataout,
       singleregister_4_dataout, singleregister_5_dataout, singleregister_6_dataout, singleregister_7_dataout;

  // Probe on {16{1'b0}}
  assign Reg1Contents = out1bit0 ? {16{1'b0}} : 16'bz;  // Controlled_Buffer controlled_buffer_1
  assign Reg2Contents = out2bit0 ? {16{1'b0}} : 16'bz;  // Controlled_Buffer controlled_buffer_2
  // Probe on singleregister_1_dataout
  singleregister singleregister_1 (
    .dataIn(WriteData), .clk(clk), .writeEnable(WE1), .reset(reset), .dataOut(singleregister_1_dataout));
  // Probe on singleregister_2_dataout
  singleregister singleregister_2 (
    .dataIn(WriteData), .clk(clk), .writeEnable(WE2), .reset(reset), .dataOut(singleregister_2_dataout));
  singleregister singleregister_3 (
    .dataIn(WriteData), .clk(clk), .writeEnable(WE3), .reset(reset), .dataOut(singleregister_3_dataout));
  // Probe on singleregister_4_dataout
  singleregister singleregister_4 (
    .dataIn(WriteData), .clk(clk), .writeEnable(WE4), .reset(reset), .dataOut(singleregister_4_dataout));
  // Probe on singleregister_5_dataout
  singleregister singleregister_5 (
    .dataIn(WriteData), .clk(clk), .writeEnable(WE5), .reset(reset), .dataOut(singleregister_5_dataout));
  // Probe on singleregister_6_dataout
  singleregister singleregister_6 (
    .dataIn(WriteData), .clk(clk), .writeEnable(WE6), .reset(reset), .dataOut(singleregister_6_dataout));
  singleregister singleregister_7 (
    .dataIn(WriteData), .clk(clk), .writeEnable(WE7), .reset(reset), .dataOut(singleregister_7_dataout));
  // Probe on {16{1'b0}}
  assign Reg1Contents = out1bit2 ? singleregister_2_dataout : 16'bz;  // Controlled_Buffer controlled_buffer_3
  assign Reg2Contents = out2bit2 ? singleregister_2_dataout : 16'bz;  // Controlled_Buffer controlled_buffer_4
  // Probe on singleregister_3_dataout
  // Probe on singleregister_4_dataout
  assign Reg1Contents = out1bit4 ? singleregister_4_dataout : 16'bz;  // Controlled_Buffer controlled_buffer_5
  assign Reg2Contents = out2bit4 ? singleregister_4_dataout : 16'bz;  // Controlled_Buffer controlled_buffer_6
  // Probe on singleregister_7_dataout
  // Probe on singleregister_1_dataout
  assign Reg1Contents = out1bit1 ? singleregister_1_dataout : 16'bz;  // Controlled_Buffer controlled_buffer_7
  assign Reg2Contents = out2bit1 ? singleregister_1_dataout : 16'bz;  // Controlled_Buffer controlled_buffer_8
  // Probe on singleregister_2_dataout
  // Probe on singleregister_3_dataout
  assign Reg1Contents = out1bit3 ? singleregister_3_dataout : 16'bz;  // Controlled_Buffer controlled_buffer_9
  assign Reg2Contents = out2bit3 ? singleregister_3_dataout : 16'bz;  // Controlled_Buffer controlled_buffer_10
  // Probe on singleregister_5_dataout
  assign Reg1Contents = out1bit5 ? singleregister_5_dataout : 16'bz;  // Controlled_Buffer controlled_buffer_11
  assign Reg2Contents = out2bit5 ? singleregister_5_dataout : 16'bz;  // Controlled_Buffer controlled_buffer_12
  // Probe on singleregister_6_dataout
  assign Reg1Contents = out1bit6 ? singleregister_6_dataout : 16'bz;  // Controlled_Buffer controlled_buffer_13
  assign Reg2Contents = out2bit6 ? singleregister_6_dataout : 16'bz;  // Controlled_Buffer controlled_buffer_14
  // Probe on singleregister_7_dataout
  assign Reg1Contents = out1bit7 ? singleregister_7_dataout : 16'bz;  // Controlled_Buffer controlled_buffer_15
  assign Reg2Contents = out2bit7 ? singleregister_7_dataout : 16'bz;  // Controlled_Buffer controlled_buffer_16
  Decoder #(.select(3)) decoder_1 (
    .out1(WE1), .out2(WE2), .out3(WE3), .out4(WE4), .out5(WE5), .out6(WE6), .out7(WE7), .sel(WritePort),
    .en(RegWriteEnable));  // open: out0
  // Probe on Reg1Contents
  Decoder #(.select(3)) decoder_2 (
    .out0(out1bit0), .out1(out1bit1), .out2(out1bit2), .out3(out1bit3), .out4(out1bit4), .out5(out1bit5),
    .out6(out1bit6), .out7(out1bit7), .sel(ReadReg1));  // open: en
  // Probe on Reg2Contents
  Decoder #(.select(3)) decoder_3 (
    .out0(out2bit0), .out1(out2bit1), .out2(out2bit2), .out3(out2bit3), .out4(out2bit4), .out5(out2bit5),
    .out6(out2bit6), .out7(out2bit7), .sel(ReadReg2));  // open: en

  // Other names for the same wires on the sheet: reg1bit0[15:0] = Reg1Contents; reg1bit1[15:0] = Reg1Contents;
  //   reg1bit2[15:0] = Reg1Contents; reg1bit3[15:0] = Reg1Contents; reg1bit4[15:0] = Reg1Contents;
  //   reg1bit5[15:0] = Reg1Contents; reg1bit6[15:0] = Reg1Contents; reg1bit7[15:0] = Reg1Contents;
  //   reg2bit0[15:0] = Reg2Contents; reg2bit1[15:0] = Reg2Contents; reg2bit2[15:0] = Reg2Contents;
  //   reg2bit3[15:0] = Reg2Contents; reg2bit4[15:0] = Reg2Contents; reg2bit5[15:0] = Reg2Contents;
  //   reg2bit6[15:0] = Reg2Contents; reg2bit7[15:0] = Reg2Contents
endmodule

module ALU (
  input  [15:0] InputData1,
  input  [15:0] InputData2,
  input  [3:0] ALUOpType,
  input  [2:0] sham,
  output [15:0] OutputData,
  output isZero,
  output rsgeqz
);

  wire [15:0] MUXadd, MUXaddi, MUXand, MUXbeq, MUXlw, MUXnot, MUXsll, MUXsrl, MUXsub, MUXsw;

  assign MUXand = InputData1 & InputData2;  // AND_Gate and_1, 16 bits wide
  assign MUXnot = ~InputData1;  // NOT_Gate not_1, 16 bits wide
  LEFTshift leftshift_1 (.sham(sham), .in1(InputData1), .out1(MUXsll));
  RIGHTshift rightshift_1 (.sham(sham), .in1(InputData1), .out1(MUXsrl));
  my_adder my_adder_1 (.B(InputData2), .A(InputData1), .sub(1'b0), .result(MUXlw));  // open: ovf
  my_adder my_adder_2 (.B(InputData2), .A(InputData1), .sub(1'b0), .result(MUXsw));  // open: ovf
  my_adder my_adder_3 (.B(InputData2), .A(InputData1), .sub(1'b1), .result(MUXbeq));  // open: ovf
  Multiplexer #(.select(4), .width(16), .enable("false")) multiplexer_1 (
    .in0(MUXaddi), .in1(MUXsub), .in2(MUXadd), .in3(MUXnot), .in4(MUXand), .in5(MUXsll), .in6(MUXsrl),
    .in7(MUXlw), .in8(MUXlw), .in9(InputData1), .in10(MUXbeq), .out(OutputData), .sel(ALUOpType));  // open: in11, in12, in13, in14, in15
  my_adder my_adder_4 (.B(InputData2), .A(InputData1), .sub(1'b0), .result(MUXaddi));  // open: ovf
  my_adder my_adder_5 (.B(InputData2), .A(InputData1), .sub(1'b1), .result(MUXsub));  // open: ovf
  my_adder my_adder_6 (.B(InputData2), .A(InputData1), .sub(1'b0), .result(MUXadd));  // open: ovf
  nor nor_1 (isZero, OutputData[0], OutputData[1], OutputData[2], OutputData[3], OutputData[4], OutputData[5], OutputData[6], OutputData[7], OutputData[9], OutputData[10], OutputData[11], OutputData[12], OutputData[13], OutputData[14], OutputData[15], OutputData[8]);

  assign rsgeqz = OutputData[15];

  // Other names for the same wires on the sheet: MUXbgez[15:0] = InputData1
endmodule

module one_bit_adder (
  input  carryin,
  input  A,
  input  B,
  output result,
  output carryout
);

  wire and_1_out, and_2_out, xor_1_out;

  and and_1 (and_1_out, B, A);
  or or_1 (carryout, and_1_out, and_2_out);
  xor xor_1 (xor_1_out, A, B);
  and and_2 (and_2_out, xor_1_out, carryin);
  xor xor_2 (result, carryin, xor_1_out);
endmodule

module my_adder (
  input  [15:0] B,
  input  [15:0] A,
  input  sub,
  output [15:0] result,
  output ovf
);

  wire one_bit_adder_1_carryout, one_bit_adder_2_carryout, one_bit_adder_3_carryout,
       one_bit_adder_4_carryout, one_bit_adder_5_carryout, one_bit_adder_6_carryout,
       one_bit_adder_7_carryout, one_bit_adder_8_carryout, one_bit_adder_9_carryout,
       one_bit_adder_10_carryout, one_bit_adder_11_carryout, one_bit_adder_12_carryout,
       one_bit_adder_13_carryout, one_bit_adder_14_carryout, one_bit_adder_15_carryout,
       one_bit_adder_16_carryout, xor_1_out, xor_2_out, xor_3_out, xor_4_out, xor_5_out, xor_6_out,
       xor_7_out, xor_8_out, xor_9_out, xor_10_out, xor_11_out, xor_12_out, xor_13_out, xor_14_out,
       xor_15_out, xor_16_out;

  xor xor_1 (xor_1_out, B[4], sub);
  xor xor_2 (xor_2_out, B[6], sub);
  xor xor_3 (xor_3_out, B[8], sub);
  xor xor_4 (xor_4_out, B[9], sub);
  xor xor_5 (xor_5_out, B[10], sub);
  xor xor_6 (xor_6_out, B[11], sub);
  xor xor_7 (xor_7_out, B[12], sub);
  xor xor_8 (xor_8_out, B[13], sub);
  xor xor_9 (xor_9_out, B[14], sub);
  xor xor_10 (xor_10_out, B[15], sub);
  xor xor_11 (xor_11_out, B[0], sub);
  xor xor_12 (xor_12_out, B[1], sub);
  xor xor_13 (xor_13_out, B[2], sub);
  xor xor_14 (xor_14_out, B[3], sub);
  xor xor_15 (xor_15_out, B[5], sub);
  xor xor_16 (xor_16_out, B[7], sub);
  one_bit_adder one_bit_adder_1 (
    .carryin(one_bit_adder_16_carryout), .A(A[6]), .B(xor_2_out), .result(result[6]),
    .carryout(one_bit_adder_1_carryout));
  one_bit_adder one_bit_adder_2 (
    .carryin(one_bit_adder_1_carryout), .A(A[7]), .B(xor_16_out), .result(result[7]),
    .carryout(one_bit_adder_2_carryout));
  one_bit_adder one_bit_adder_3 (
    .carryin(one_bit_adder_2_carryout), .A(A[8]), .B(xor_3_out), .result(result[8]),
    .carryout(one_bit_adder_3_carryout));
  one_bit_adder one_bit_adder_4 (
    .carryin(one_bit_adder_3_carryout), .A(A[9]), .B(xor_4_out), .result(result[9]),
    .carryout(one_bit_adder_4_carryout));
  one_bit_adder one_bit_adder_5 (
    .carryin(one_bit_adder_4_carryout), .A(A[10]), .B(xor_5_out), .result(result[10]),
    .carryout(one_bit_adder_5_carryout));
  one_bit_adder one_bit_adder_6 (
    .carryin(one_bit_adder_5_carryout), .A(A[11]), .B(xor_6_out), .result(result[11]),
    .carryout(one_bit_adder_6_carryout));
  one_bit_adder one_bit_adder_7 (
    .carryin(one_bit_adder_6_carryout), .A(A[12]), .B(xor_7_out), .result(result[12]),
    .carryout(one_bit_adder_7_carryout));
  one_bit_adder one_bit_adder_8 (
    .carryin(one_bit_adder_7_carryout), .A(A[13]), .B(xor_8_out), .result(result[13]),
    .carryout(one_bit_adder_8_carryout));
  one_bit_adder one_bit_adder_9 (
    .carryin(one_bit_adder_8_carryout), .A(A[14]), .B(xor_9_out), .result(result[14]),
    .carryout(one_bit_adder_9_carryout));
  one_bit_adder one_bit_adder_10 (
    .carryin(one_bit_adder_9_carryout), .A(A[15]), .B(xor_10_out), .result(result[15]),
    .carryout(one_bit_adder_10_carryout));
  one_bit_adder one_bit_adder_11 (
    .carryin(sub), .A(A[0]), .B(xor_11_out), .result(result[0]), .carryout(one_bit_adder_11_carryout));
  one_bit_adder one_bit_adder_12 (
    .carryin(one_bit_adder_11_carryout), .A(A[1]), .B(xor_12_out), .result(result[1]),
    .carryout(one_bit_adder_12_carryout));
  one_bit_adder one_bit_adder_13 (
    .carryin(one_bit_adder_12_carryout), .A(A[2]), .B(xor_13_out), .result(result[2]),
    .carryout(one_bit_adder_13_carryout));
  one_bit_adder one_bit_adder_14 (
    .carryin(one_bit_adder_13_carryout), .A(A[3]), .B(xor_14_out), .result(result[3]),
    .carryout(one_bit_adder_14_carryout));
  one_bit_adder one_bit_adder_15 (
    .carryin(one_bit_adder_14_carryout), .A(A[4]), .B(xor_1_out), .result(result[4]),
    .carryout(one_bit_adder_15_carryout));
  one_bit_adder one_bit_adder_16 (
    .carryin(one_bit_adder_15_carryout), .A(A[5]), .B(xor_15_out), .result(result[5]),
    .carryout(one_bit_adder_16_carryout));
  xor xor_17 (ovf, one_bit_adder_9_carryout, one_bit_adder_10_carryout);

  // Other names for the same wires on the sheet: A1 = A[0]; A2 = A[1]; A3 = A[2]; A4 = A[3]; A5 = A[4]; A6 = A[5];
  //   A7 = A[6]; A8 = A[7]; A9 = A[8]; A10 = A[9]; A11 = A[10]; A12 = A[11]; A13 = A[12]; A14 = A[13]; A15 = A[14];
  //   A16 = A[15]; B1 = B[0]; B2 = B[1]; B3 = B[2]; B4 = B[3]; B5 = B[4]; B6 = B[5]; B7 = B[6]; B8 = B[7]; B9 = B[8];
  //   B10 = B[9]; B11 = B[10]; B12 = B[11]; B13 = B[12]; B14 = B[13]; B15 = B[14]; B16 = B[15]; r1 = result[0];
  //   r2 = result[1]; r3 = result[2]; r4 = result[3]; r5 = result[4]; r6 = result[5]; r7 = result[6]; r8 = result[7];
  //   r9 = result[8]; r10 = result[9]; r11 = result[10]; r12 = result[11]; r13 = result[12]; r14 = result[13];
  //   r15 = result[14]; r16 = result[15]
endmodule

module LEFTshift (
  input  [2:0] sham,
  input  [15:0] in1,
  output [15:0] out1
);

  wire sham0, sham1, sham2;
  wire [15:0] multiplexer_1_out;
  wire [15:4] multiplexer_2_out_2;
  wire [15:12] multiplexer_2_out;

  and and_1 (sham0, 1'b1, sham[0]);
  and and_2 (sham1, 1'b1, sham[1]);
  and and_3 (sham2, 1'b1, sham[2]);
  Multiplexer #(.width(16), .enable("false")) multiplexer_1 (
    .in0(in1), .in1({in1[14:0], 1'b0}), .out(multiplexer_1_out), .sel(sham0));
  Multiplexer #(.width(16), .enable("false")) multiplexer_2 (
    .in0(multiplexer_1_out), .in1({multiplexer_1_out[13:0], 2'b00}),
    .out({multiplexer_2_out, multiplexer_2_out_2}), .sel(sham1));
  Multiplexer #(.width(16), .enable("false")) multiplexer_3 (
    .in0({multiplexer_2_out, multiplexer_2_out_2}), .in1({multiplexer_2_out_2, 4'b0000}), .out(out1),
    .sel(sham2));
endmodule

module PC (
  input  reset,
  input  [15:0] nextPC,
  input  [15:0] currentPC
);
endmodule

module memory_latch (
  input  [15:0] address,
  input  WE,
  input  clk,
  input  [15:0] data_in,
  output [15:0] address_latched,
  output WE_latched,
  output OE_latched,
  output [15:0] data_in_latched
);

  wire DMwe_latch_q;
  wire [15:0] addr_latch_q;

  Register #(.width(16), .trigger("falling")) addr_latch (
    .D(address), .en(WE), .clk(clk), .Q(addr_latch_q));  // open: clr
  D_Flip_Flop #(.trigger("falling")) DMwe_latch (.D(WE), .clk(clk), .Q(DMwe_latch_q));  // open: Qn, preset, reset
  Register #(.width(16), .trigger("falling")) data_to_be_written (
    .D(data_in), .en(WE), .clk(clk), .Q(data_in_latched));  // open: clr
  Multiplexer #(.width(16), .enable("false")) multiplexer_1 (
    .in0(address), .in1(addr_latch_q), .out(address_latched), .sel(DMwe_latch_q));
  and and_1 (WE_latched, clk, DMwe_latch_q);
  not not_1 (OE_latched, WE_latched);
endmodule

module RIGHTshift (
  input  [2:0] sham,
  input  [15:0] in1,
  output [15:0] out1
);

  wire sham0, sham1, sham2;
  wire [3:0] multiplexer_2_out;
  wire [11:0] multiplexer_2_out_2;
  wire [15:0] multiplexer_1_out;

  and and_1 (sham0, 1'b1, sham[0]);
  and and_2 (sham1, 1'b1, sham[1]);
  and and_3 (sham2, 1'b1, sham[2]);
  Multiplexer #(.width(16), .enable("false")) multiplexer_1 (
    .in0(in1), .in1({1'b0, in1[15:1]}), .out(multiplexer_1_out), .sel(sham0));
  Multiplexer #(.width(16), .enable("false")) multiplexer_2 (
    .in0(multiplexer_1_out), .in1({2'b00, multiplexer_1_out[15:2]}),
    .out({multiplexer_2_out_2, multiplexer_2_out}), .sel(sham1));
  Multiplexer #(.width(16), .enable("false")) multiplexer_3 (
    .in0({multiplexer_2_out_2, multiplexer_2_out}), .in1({4'b0000, multiplexer_2_out_2}), .out(out1),
    .sel(sham2));
endmodule
